# Fritzing sketch Artnet DMX Converter (saved by Fritzing 1.0.4)
circuit board: 9cm x 8cm
perfboards: 1

parts:
  XLR1 = XLR NC3MAAH [package=nc3maah]
  XLR2 = XLR NC3MAAH [package=nc3maah]
  C2_100nF = Capacitor [package=cap-pth-5mm]
  C3_100nF = Capacitor [package=cap-pth-5mm]
  X1 = USB Connectors [package=usb-microb]
  Squix1 = OLED 0.96" 128x64 I2C SSD1306
  M1 = MAX485 Breakout [package=THT]
  M2 = MAX485 Breakout [package=THT]
  C2_100nF1 = Capacitor [package=cap-pth-5mm]
  R2 = Resistor [tolerance=±5% power=0.25W resistance=10k package=THT]
  U1 = LuaNode32 / ESP32 [part_number=ESP32S-PIN30]
  C1 = Electrolytic Capacitor [capacitance=1mF voltage=35V package="100 mil [THT, electrolytic]"]
  W5500_Module1 = W5500 Ethernet module [package="DIP (Dual Inline) [THT]"]
  A1 = AMS11176 module
  C3_100nF1 = Capacitor [package=cap-pth-5mm]
  C2 = Electrolytic Capacitor [capacitance=50µF voltage=35V package="100 mil [THT, electrolytic]"]
  R3 = Resistor [tolerance=±5% power=0.25W resistance=10k package=THT]

nets:
  GND: XLR1.1, XLR1.G, XLR2.1, XLR2.G, C2_100nF.1, C3_100nF.1, X1.GND, Squix1.GND, M1.GND, M2.GND, C2_100nF1.2, R2.Pin_0, U1.GND, C1.+, W5500_Module1.GND, A1.pin3, C3_100nF1.1, C2.+, R3.Pin_0
  N1: XLR1.2, M1.B
  N2: XLR1.3, M1.A, M1.A1
  N3: XLR2.2, M2.B, M2.B1
  N4: XLR2.3, M2.A, M2.A1
  VCC: C2_100nF.2, C3_100nF.2, X1.VBUS, Squix1.VCC, M1.VCC, M2.VCC, C2_100nF1.1, U1.Vin, C1.-, A1.pin1
  N5: Squix1.SCL, U1.D22
  N6: Squix1.SCA, U1.D21
  N7: M1.RO, U1.D26
  N8: M1.RE, M1.DE, R2.Pin_1, U1.D13
  N9: M1.DI, U1.D25
  N10: M2.RO, U1.D18
  N11: M2.RE, M2.DE, U1.D32, R3.Pin_1
  N12: M2.DI, U1.D19
  N13: U1.D33, W5500_Module1.MISO
  N14: U1.D27, W5500_Module1.MOSI
  N15: U1.D14, W5500_Module1.SCLK
  N16: U1.D15, W5500_Module1.SCS
  N17: U1.D4, W5500_Module1.RST
  N18: W5500_Module1.5V, A1.pin2, C3_100nF1.2, C2.-

custom parts:
  MAX485 Breakout: MAX485 RS485 breakout board
  LuaNode32 / ESP32: New Image for LuaNode32 DOIT ESP32 DEVKIT V1. Base parts from LuaNode32 / ESP32 ESP32 based LuaNode32 by G.Noorlander DOIT Esp32 DevKit v1 (30 pins long, 11 pins width) by Werner Rothschopf (modified by vanepp Dec 2018)
  W5500 Ethernet module: W5500 based SPI Ethernet module for Arduino, etc.
  AMS11176 module: DC-DC step-down modules ( input DC 4.5～7V , output DC 3.3V ).
